# Fritzing sketch Fritz_scketch (saved by Fritzing 0.9.3b)

parts:
  U1 = ESP8266 WiFi Module [part_number=ESP8266]
  KY-1 = Keyes Relay [package=THT]
  IR1 = TSOP312.., 314.. [package=THT]
  Q1 = LTR-301 [package=ltr-301]

nets:
  N1: U1.IO2, IR1.Data
  3.3V: U1.3.3V, IR1.Vs
  GND: U1.GND, KY-1.ground, IR1.GND, Q1.C
  N2: U1.IO14, KY-1.signal
  N3: U1.IO15, Q1.E
  5V: KY-1.power
  N4: KY-1.NC, KY-1.C, KY-1.NO

custom parts:
  Keyes Relay: The Keyes 5V relay module is suitable for SCM development, home appliance control. It uses a 5V~12V TIL control signal which can control DC / AC signal.
